# Fritzing sketch Fritzing_Stazione_Meteo_De_Luca (saved by Fritzing 0.9.3b)
breadboards: 1

parts:
  Display_LCD_l2C = Grove OLED 128x96
  Humidity = Humidity Sensor - HIH-4030 Breakout
  Photoresistor = Photocell (LDR) [package=THT]
  Arduino_UNO_R3_+_shield = Arduino Ethernet Shield (Rev3)
  Temperature = TMP36 Temperature Sensor [package="TO92 [THT]"]
  R1_10K = Resistor [tolerance=±5% resistance=10 package="0402 [SMD]"]
  Pressure = Barometric Pressure Sensor - BMP180 Breakout (GY-68)

nets:
  GND: Display_LCD_l2C.GND, Humidity.GND, Arduino_UNO_R3_+_shield.GND, Temperature.GND, R1_10K.Pin_1, Pressure.GND
  VCC: Display_LCD_l2C.VCC, Arduino_UNO_R3_+_shield.5V
  N1: Display_LCD_l2C.SDA, Arduino_UNO_R3_+_shield.A4/SDA, Pressure.SDA
  N2: Display_LCD_l2C.SCL, Arduino_UNO_R3_+_shield.A5/SCL, Pressure.SCL
  N3: Humidity.OUT, Arduino_UNO_R3_+_shield.A2
  VCC_2: Humidity.VCC, Photoresistor.pin_0, Arduino_UNO_R3_+_shield.3V3, Temperature.+Vs, Pressure.VCC
  N4: Photoresistor.pin_1, Arduino_UNO_R3_+_shield.A0, R1_10K.Pin_0
  N5: Arduino_UNO_R3_+_shield.A1, Temperature.Vout
